// Logisim project ex4.circ as structural Verilog: 1 circuit, main circuit Split
module Split (
  input  [7:0] In1,
  output Out1,
  output [7:0] Out2
);

  not not_1 (Out2[7], In1[7]);
  and and_1 (Out1, In1[0], In1[7]);

  assign Out2[6:0] = In1[6:0];

  // Notes on the sheet:
  //   hint:out1=1->first and last bit 1->negative odd int
  //   take the input and interpret as 2's complement, what input will have ouput1 =1?
  //   PUT CIRCUITRY HERE
  //   sign and magnitude
endmodule
